// Logisim project 4bitcomparator.circ as structural Verilog: 5 circuits, main circuit 4 bit a>b
module _4_bit_a_b (
  input  [3:0] input_A,
  input  [3:0] input_B,
  output A_B
);

  wire and_1_out, and_2_out, and_3_out, and_4_out, not_1_out, not_2_out, not_3_out, xor_1_out, xor_2_out,
       xor_3_out, xor_4_out;

  xor xor_1 (xor_1_out, input_A[3], input_B[3]);
  xor xor_2 (xor_2_out, input_A[2], input_B[2]);
  xor xor_3 (xor_3_out, input_A[1], input_B[1]);
  xor xor_4 (xor_4_out, input_A[0], input_B[0]);
  not not_1 (not_1_out, xor_1_out);
  not not_2 (not_2_out, xor_2_out);
  not not_3 (not_3_out, xor_3_out);
  and and_1 (and_1_out, input_A[3], xor_1_out);
  and and_2 (and_2_out, not_1_out, input_A[2], xor_2_out);
  and and_3 (and_3_out, not_1_out, not_2_out, input_A[1], xor_3_out);
  and and_4 (and_4_out, not_1_out, not_2_out, not_3_out, xor_4_out, input_A[0]);
  or or_1 (A_B, and_1_out, and_2_out, and_3_out, and_4_out);
endmodule

module _4_bit_a_b_2 (
  input  [3:0] in_1,
  input  [3:0] in_2,
  output out_3
);

  wire and_1_out, and_2_out, and_3_out, and_4_out, not_1_out, not_2_out, not_3_out, xor_1_out, xor_2_out,
       xor_3_out, xor_4_out;

  xor xor_1 (xor_1_out, in_1[3], in_2[3]);
  not not_1 (not_1_out, xor_1_out);
  xor xor_2 (xor_2_out, in_1[2], in_2[2]);
  not not_2 (not_2_out, xor_2_out);
  xor xor_3 (xor_3_out, in_1[1], in_2[1]);
  not not_3 (not_3_out, xor_3_out);
  xor xor_4 (xor_4_out, in_1[0], in_2[0]);
  and and_1 (and_1_out, in_2[3], xor_1_out);
  and and_2 (and_2_out, not_1_out, in_2[2], xor_2_out);
  and and_3 (and_3_out, not_1_out, not_2_out, in_2[1], xor_3_out);
  and and_4 (and_4_out, not_1_out, not_2_out, not_3_out, xor_4_out, in_2[0]);
  or or_1 (out_3, and_1_out, and_2_out, and_3_out, and_4_out);
endmodule

module combined (
  input  [3:0] A,
  input  [3:0] B,
  output A_B,
  output A_B_2,
  output A_B_3
);

  _4_bit_a_b u_4_bit_a_b_1 (.A_B(A_B), .input_A(A), .input_B(B));
  _4_bit_a_b u_4_bit_a_b_2 (.A_B(A_B_3), .input_A(B), .input_B(A));
  nor nor_1 (A_B_2, A_B, A_B_3);

  // Notes on the sheet:
  //   A>B
  //   reversed the wiring
endmodule

module memory (
  input  [3:0] INPUT,
  input  in_2,
  input  in_3,
  output [3:0] OUTPUT
);

  wire n4_bit_a_b_1_a_b;

  Register #(.width(4), .trigger("high")) register_1 (
    .D(INPUT), .en(in_2), .Q(OUTPUT), .clk(n4_bit_a_b_1_a_b), .clr(in_3));
  _4_bit_a_b u_4_bit_a_b_1 (.A_B(n4_bit_a_b_1_a_b), .input_A(INPUT), .input_B(OUTPUT));
endmodule

module FINAL (
  input  [3:0] INPUT,
  output [3:0] GREATEST_NUMBER
);

  wire ENABLE_out, RESET_out;

  Button ENABLE (.out(ENABLE_out));
  memory memory_1 (.INPUT(INPUT), .OUTPUT(GREATEST_NUMBER), .in_2(ENABLE_out), .in_3(RESET_out));
  Button RESET (.out(RESET_out));
endmodule
